# Fritzing sketch Water level sensor (saved by Fritzing 0.9.4)
breadboards: 1

parts:
  Parça1 = Arduino Uno (Rev3)
  R1 = Resistor [tolerance=±5% resistance=330 package="2512 [SMD]"]
  LED1 = smd LED [color="Red (633nm)" package="0805 [SMD]"]
  J1 = Piezo Speaker
  R2 = Resistor [tolerance=±5% resistance=330 package="2512 [SMD]"]
  Water_Level_Sensor1 = Water Level Sensor

nets:
  N1: Parça1.A0, Water_Level_Sensor1.SIG
  N2: Parça1.D8, R1.Pin_0
  N3: Parça1.D9_PWM, R2.Pin_1
  GND: Parça1.GND, LED1.cathode, J1.pin1, Water_Level_Sensor1.GND
  5V: Parça1.5V, Water_Level_Sensor1.VCC
  N4: R1.Pin_1, LED1.anode
  N5: J1.pin2, R2.Pin_0

custom parts:
  Water Level Sensor: A water level sensor. This sensor operates at 3V to 5V. The Sig (signal) pin outputs an analogue signal that is in proportion to the amount of water in contact with the sensor.
